# Fritzing sketch Tranxen200Pad (saved by Fritzing 0.8.7b)
stripboards: 1

parts:
  Composant3 = DB25F  # not connected
  J1 = Piezo Speaker
  J2 = Piezo Speaker
  J3 = Piezo Speaker
  J4 = Piezo Speaker
  J5 = Piezo Speaker
  J6 = Piezo Speaker
  J7 = Piezo Speaker
  J8 = Piezo Speaker
  J9 = Piezo Speaker
  LED1 = LED - 5mm [color="Red (633nm)" package="5 mm [THT]"]
  LED2 = LED - 5mm [color="Red (633nm)" package="5 mm [THT]"]
  LED3 = LED - 5mm [color="Red (633nm)" package="5 mm [THT]"]
  LED4 = LED - 5mm [color="Red (633nm)" package="5 mm [THT]"]
  LED5 = LED - 5mm [color="Red (633nm)" package="5 mm [THT]"]
  LED6 = LED - 5mm [color="Red (633nm)" package="5 mm [THT]"]
  LED7 = LED - 5mm [color="Red (633nm)" package="5 mm [THT]"]
  LED8 = LED - 5mm [color="Red (633nm)" package="5 mm [THT]"]
  LED9 = LED - 5mm [color="Red (633nm)" package="5 mm [THT]"]
  LED10 = LED - 5mm [color="Red (633nm)" package="5 mm [THT]"]
  R1 = Resistor [tolerance=±5% resistance=1M package=THT]
  D1 = Rectifier Diode [part_number=1N4001 package="300 mil [THT]"]
  D2 = Rectifier Diode [part_number=1N4001 package="300 mil [THT]"]
  R3 = Resistor [tolerance=±5% resistance=1M package=THT]
  D4 = Rectifier Diode [part_number=1N4001 package="300 mil [THT]"]
  D3 = Rectifier Diode [part_number=1N4001 package="300 mil [THT]"]
  R4 = Resistor [tolerance=±5% resistance=1M package=THT]
  R5 = Resistor [tolerance=±5% resistance=1M package=THT]
  R6 = Resistor [tolerance=±5% resistance=1M package=THT]
  R7 = Resistor [tolerance=±5% resistance=1M package=THT]
  D6 = Rectifier Diode [part_number=1N4001 package="300 mil [THT]"]
  D7 = Rectifier Diode [part_number=1N4001 package="300 mil [THT]"]
  R8 = Resistor [tolerance=±5% resistance=1M package=THT]
  R9 = Resistor [tolerance=±5% resistance=1M package=THT]
  R10 = Resistor [tolerance=±5% resistance=1M package=THT]
  D8 = Rectifier Diode [part_number=1N4001 package="300 mil [THT]"]
  D9 = Rectifier Diode [part_number=1N4001 package="300 mil [THT]"]
  D10 = Rectifier Diode [part_number=1N4001 package="300 mil [THT]"]
  J10 = Piezo Speaker
  R11 = Resistor [tolerance=±5% resistance=1k package=THT]
  R12 = Resistor [tolerance=±5% resistance=1k package=THT]
  R13 = Resistor [tolerance=±5% resistance=1k package=THT]
  R14 = Resistor [tolerance=±5% resistance=1k package=THT]
  R15 = Resistor [tolerance=±5% resistance=1k package=THT]
  R16 = Resistor [tolerance=±5% resistance=1k package=THT]
  R17 = Resistor [tolerance=±5% resistance=1k package=THT]
  R18 = Resistor [tolerance=±5% resistance=1k package=THT]
  R19 = Resistor [tolerance=±5% resistance=1k package=THT]
  R20 = Resistor [tolerance=±5% resistance=1k package=THT]
  D5 = Rectifier Diode [part_number=1N4001 package="300 mil [THT]"]
  R21 = Resistor [tolerance=±5% resistance=1M package=THT]
  Threshold = mystery part, 3 pins [chip_label=?]  # not connected
  Relax-Delay = mystery part, 3 pins [chip_label=?]  # not connected
  S1 = Pushbutton [package=THT]  # not connected
  R22 = Resistor [tolerance=±5% resistance=10k package=THT]

nets:
  N1: J1.pin1, J2.pin1, J3.pin1, J4.pin1, J5.pin1, J6.pin1, J7.pin1, J8.pin1, J9.pin1, LED1.cathode, LED2.cathode, LED3.cathode, LED4.cathode, LED5.cathode, LED6.cathode, LED7.cathode, LED8.cathode, LED9.cathode, LED10.cathode, R1.Pin_0, D1.anode, D2.anode, R3.Pin_0, D4.anode, D3.anode, R4.Pin_0, R5.Pin_0, R6.Pin_0, R7.Pin_0, D6.anode, D7.anode, R8.Pin_0, R9.Pin_0, R10.Pin_0, D8.anode, D9.anode, D10.anode, J10.pin1, D5.anode, R21.Pin_0, R22.Pin_1
  N2: J1.pin2, R1.Pin_1, D1.cathode
  N3: J2.pin2, D2.cathode, R5.Pin_1
  N4: J3.pin2, R3.Pin_1, D3.cathode
  N5: J4.pin2, D4.cathode, R4.Pin_1
  N6: J5.pin2, R6.Pin_1, D5.cathode
  N7: J6.pin2, D6.cathode, R9.Pin_1
  N8: J7.pin2, R7.Pin_1, D7.cathode
  N9: J8.pin2, R10.Pin_1, D8.cathode
  N10: J9.pin2, R8.Pin_1, D9.cathode
  N11: LED1.anode, R11.Pin_1
  N12: LED2.anode, R12.Pin_1
  N13: LED3.anode, R13.Pin_1
  N14: LED4.anode, R14.Pin_1
  N15: LED5.anode, R15.Pin_1
  N16: LED6.anode, R16.Pin_1
  N17: LED7.anode, R17.Pin_1
  N18: LED8.anode, R18.Pin_1
  N19: LED9.anode, R19.Pin_1
  N20: LED10.anode, R20.Pin_1
  N21: D10.cathode, J10.pin2, R21.Pin_1
